# Fritzing sketch fritzing-schematic (saved by Fritzing 0.9.6b)
breadboards: 1

parts:
  Part1 = Arduino Uno (Rev3)
  Part2 = Adafruit LSM9DS1 9DoF Breakout [part_number="Adafruit #3387"]
  Part3 = Adafruit LSM9DS1 9DoF Breakout [part_number="Adafruit #3387"]
  Part4 = Adafruit LSM9DS1 9DoF Breakout [part_number="Adafruit #3387"]

nets:
  N1: Part1.D8, Part4.CS_AG
  N2: Part1.D9_PWM, Part4.CS_MAG
  N3: Part1.D13/SCK, Part2.SCL, Part3.SCL, Part4.SCL
  GND: Part1.GND, Part4.GND
  N4: Part1.D2, Part2.CS_AG
  N5: Part1.D3_PWM, Part2.CS_MAG
  N6: Part1.D6_PWM, Part3.CS_AG
  N7: Part1.D7, Part3.CS_MAG
  VIN: Part1.VIN, Part2.VIN, Part3.VIN, Part4.VIN
  N8: Part2.SDA, Part3.SDA, Part4.SDA

custom parts:
  Adafruit LSM9DS1 9DoF Breakout: Add motion, direction and orientation sensing to your Arduino project with this all-in-one 9-DOF sensor. Inside the chip are three sensors, one is a classic 3-axis accelerometer, which can tell you which direction is down towards the Earth (by measuring gravity) or how fast the board is accelerating in 3D space. The other is a 3-axis magnetometer that can sense where the strongest magnetic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
